// Logisim project Logisim-131-207.circ as structural Verilog: 5 circuits, main circuit main
module main (
  input  P3,
  input  P2,
  input  P1,
  input  P0,
  input  G3,
  input  G2,
  input  G1,
  input  G0,
  input  B0,
  input  S0,
  input  in_11,
  input  B1,
  input  B2,
  input  S1,
  input  B3,
  input  I0,
  input  I1,
  input  I2,
  input  I3,
  input  clear,
  input  enable,
  input  clear_2,
  input  enable_2,
  input  in_24,
  input  in_25,
  input  in_26,
  input  in_27,
  output T1,
  output F3,
  output F2,
  output F1,
  output F0,
  output out_33,
  output T2
);

  wire and_1_out, clock_1_out, clock_2_out, d_ff_1_q, d_ff_2_q, d_ff_3_q, d_ff_4_q, d_ff_5_q, d_ff_6_q,
       d_ff_7_q, d_ff_8_q, MAG_COMP_2_a___b, MAG_COMP_2_a_b, MAG_COMP_a___b, MAG_COMP_a___b_2, MAG_COMP_a_b,
       multiplexer_1_o, or_1_out, paralleladder_1_s0, paralleladder_1_s1, paralleladder_1_s2,
       paralleladder_1_s3;

  paralleladder paralleladder_1 (
    .B3(d_ff_4_q), .A3(in_11), .B2(d_ff_3_q), .A2(in_11), .B1(d_ff_2_q), .A1(in_11), .B0(d_ff_1_q),
    .A0(or_1_out), .s3(paralleladder_1_s3), .s2(paralleladder_1_s2), .s1(paralleladder_1_s1),
    .S0(paralleladder_1_s0), .M(in_11));  // open: out_10
  Clock clock_1 (.out(clock_1_out));
  or or_1 (or_1_out, MAG_COMP_a___b_2, MAG_COMP_a___b);
  D_Flip_Flop d_ff_1 (
    .clk(clock_1_out), .D(paralleladder_1_s0), .Q(d_ff_1_q), .en(enable_2), .reset(clear_2));  // open: Qn, preset
  D_Flip_Flop d_ff_2 (
    .clk(clock_1_out), .D(paralleladder_1_s1), .Q(d_ff_2_q), .en(enable_2), .reset(clear_2));  // open: Qn, preset
  D_Flip_Flop d_ff_3 (
    .clk(clock_1_out), .D(paralleladder_1_s2), .Q(d_ff_3_q), .en(enable_2), .reset(clear_2));  // open: Qn, preset
  D_Flip_Flop d_ff_4 (
    .clk(clock_1_out), .D(paralleladder_1_s3), .Q(d_ff_4_q), .en(enable_2), .reset(clear_2));  // open: Qn, preset
  magnitude MAG_COMP (
    .A3(G3), .B3(P3), .A2(G2), .B2(P2), .A1(G1), .B1(P1), .A0(G0), .B0(P0), .A___B(MAG_COMP_a___b),
    .A___B_2(MAG_COMP_a___b_2), .A_B(MAG_COMP_a_b));
  and and_1 (and_1_out, T1, MAG_COMP_a_b);
  or or_2 (T1, MAG_COMP_2_a___b, MAG_COMP_2_a_b);
  magnitude MAG_COMP_2 (
    .A3(d_ff_4_q), .B3(in_24), .A2(d_ff_3_q), .B2(in_25), .A1(d_ff_2_q), .B1(in_26), .A0(d_ff_1_q),
    .B0(in_27), .A___B(MAG_COMP_2_a___b), .A_B(MAG_COMP_2_a_b));  // open: A___B_2
  multiplexer multiplexer_1 (
    .s0(S0), .s1(S1), .I0(I0), .I1(I1), .I2(I2), .I3(I3), .enable(and_1_out), .O(multiplexer_1_o));
  Clock clock_2 (.out(clock_2_out));
  paralleladder paralleladder_2 (
    .out_10(out_33), .B3(B3), .A3(d_ff_5_q), .B2(B2), .A2(d_ff_6_q), .B1(B1), .A1(d_ff_7_q), .B0(B0),
    .A0(d_ff_8_q), .s3(F3), .s2(F2), .s1(F1), .S0(F0), .M(multiplexer_1_o));
  D_Flip_Flop d_ff_5 (.clk(clock_2_out), .D(F3), .Q(d_ff_5_q), .en(enable), .reset(clear));  // open: Qn, preset
  D_Flip_Flop d_ff_6 (.clk(clock_2_out), .D(F2), .Q(d_ff_6_q), .en(enable), .reset(clear));  // open: Qn, preset
  D_Flip_Flop d_ff_7 (.clk(clock_2_out), .D(F1), .Q(d_ff_7_q), .en(enable), .reset(clear));  // open: Qn, preset
  D_Flip_Flop d_ff_8 (.clk(clock_2_out), .D(F0), .Q(d_ff_8_q), .en(enable), .reset(clear));  // open: Qn, preset
  magnitude MAG_COMP_3 (
    .A3(B3), .B3(d_ff_5_q), .A2(B2), .B2(d_ff_6_q), .A1(B1), .B1(d_ff_7_q), .A0(B0), .B0(d_ff_8_q),
    .A___B_2(T2));  // open: A___B, A_B

  // Notes on the sheet:
  //   PREFED PIN
  //   add/sub
  //   CLOCK PULSE
  //   PASSWORD (to be entered by the user )
  //   It counts number of invalid
  //   inputs
  //   INCORRECT
  //   MINI ATM MACHINE
  //   16CO131-
  //   PASSWORD
  //   16CO207
  //   CORRECT PIN
  //              deposit 00
  //   withdrawal 01
  //   ACCORDING TO MENTIONED 
  //   select line
  //   select line
  //   IF THIS SIGNAL IS LOW THEN 
  //   NUMBER OF WRONG INPUTS 
  //   ALREADY REACHED 3
  //   SO TAKING INPUT IS AVOIDED
  //   THE PROCESS IS TERMINATED
  //   if the number
  //   CONDITIONS
  //   MUX
  //   MSB
  //   CLOCK PULSE
  //   the user can go for a next trial
  //   (amount to be withdrawn or deposited)
  //   of wrong inputs is less than or equal to 3
  //   add/sub
  //     FINAL BALANCE
  //   IN THE ACCOUNT
  //   IF THIS SIGNAL IS HIGH
  //   THEN WITHDRAWAL IS NOT
  //   POSSIBLE
  //   The balance is restricted
  //   to 4 bit binary number
endmodule

module magnitude (
  input  A3,
  input  B3,
  input  A2,
  input  B2,
  input  A1,
  input  B1,
  input  A0,
  input  B0,
  output A___B,
  output A___B_2,
  output A_B
);

  wire and_1_out, and_2_out, and_3_out, and_4_out, and_5_out, and_6_out, and_7_out, and_8_out, and_9_out,
       and_10_out, and_11_out, and_12_out, and_13_out, and_14_out, nor_1_out, nor_2_out, nor_3_out,
       nor_4_out, not_1_out, not_2_out, not_3_out, not_4_out, not_5_out, not_6_out, not_7_out, not_8_out;

  not not_1 (not_1_out, A3);
  not not_2 (not_2_out, B3);
  not not_3 (not_3_out, A2);
  not not_4 (not_4_out, B2);
  not not_5 (not_5_out, A1);
  not not_6 (not_6_out, B1);
  not not_7 (not_7_out, A0);
  not not_8 (not_8_out, B0);
  and and_1 (and_1_out, not_1_out, B3);
  and and_2 (and_2_out, A3, not_2_out);
  and and_3 (and_3_out, not_3_out, B2);
  and and_4 (and_4_out, A2, not_4_out);
  and and_5 (and_5_out, not_5_out, B1);
  and and_6 (and_6_out, A1, not_6_out);
  and and_7 (and_7_out, not_7_out, B0);
  and and_8 (and_8_out, A0, not_8_out);
  nor nor_1 (nor_1_out, and_1_out, and_2_out);
  nor nor_2 (nor_2_out, and_3_out, and_4_out);
  nor nor_3 (nor_3_out, and_5_out, and_6_out);
  nor nor_4 (nor_4_out, and_7_out, and_8_out);
  and and_9 (and_9_out, nor_1_out, and_3_out);
  and and_10 (and_10_out, nor_1_out, and_4_out);
  and and_11 (and_11_out, nor_1_out, nor_2_out, and_5_out);
  and and_12 (and_12_out, nor_1_out, nor_2_out, and_6_out);
  and and_13 (and_13_out, nor_1_out, nor_2_out, nor_3_out, and_7_out);
  and and_14 (and_14_out, nor_1_out, nor_2_out, nor_3_out, and_8_out);
  and and_15 (A_B, nor_1_out, nor_4_out, nor_2_out, nor_3_out);
  or or_1 (A___B, and_1_out, and_9_out, and_11_out, and_13_out);
  or or_2 (A___B_2, and_2_out, and_14_out, and_12_out, and_10_out);

  // Notes on the sheet:
  //   4 BIT MAGNITUDE COMPARATOR
endmodule

module multiplexer (
  input  s0,
  input  s1,
  input  enable,
  input  I0,
  input  I1,
  input  I2,
  input  I3,
  output O
);

  wire and_1_out, and_2_out, and_3_out, and_4_out, not_1_out, not_2_out;

  not not_1 (not_1_out, s0);
  not not_2 (not_2_out, s1);
  and and_1 (and_1_out, I0, not_2_out, enable, not_1_out);
  and and_2 (and_2_out, enable, I1, s1, not_1_out);
  and and_3 (and_3_out, I2, not_2_out, enable, s0);
  and and_4 (and_4_out, I3, s1, enable, s0);
  or or_1 (O, and_1_out, and_2_out, and_3_out, and_4_out);

  // Notes on the sheet:
  //   Multiplexer
endmodule

module paralleladder (
  input  B3,
  input  A3,
  input  B2,
  input  A2,
  input  B1,
  input  A1,
  input  B0,
  input  A0,
  input  M,
  output out_10,
  output s3,
  output s2,
  output s1,
  output S0
);

  wire fulladder_2_out_5, fulladder_3_out_5, fulladder_4_out_5, xor_1_out, xor_2_out, xor_3_out, xor_4_out;

  xor xor_1 (xor_1_out, B3, M);
  fulladder fulladder_1 (.C(fulladder_2_out_5), .A(A3), .B(xor_1_out), .out_4(s3), .out_5(out_10));
  xor xor_2 (xor_2_out, B2, M);
  fulladder fulladder_2 (.C(fulladder_3_out_5), .A(A2), .B(xor_2_out), .out_4(s2), .out_5(fulladder_2_out_5));
  xor xor_3 (xor_3_out, B1, M);
  fulladder fulladder_3 (.C(fulladder_4_out_5), .A(A1), .B(xor_3_out), .out_4(s1), .out_5(fulladder_3_out_5));
  xor xor_4 (xor_4_out, B0, M);
  fulladder fulladder_4 (.C(M), .A(A0), .B(xor_4_out), .out_4(S0), .out_5(fulladder_4_out_5));

  // Notes on the sheet:
  //   cout
  //   PARALLEL ADDER SUBTRACTOR
endmodule

module fulladder (
  input  C,
  input  A,
  input  B,
  output out_4,
  output out_5
);

  wire and_1_out, and_2_out, xor_1_out;

  xor xor_1 (xor_1_out, A, B);
  and and_1 (and_1_out, A, B);
  xor xor_2 (out_4, C, xor_1_out);
  and and_2 (and_2_out, C, xor_1_out);
  or or_1 (out_5, and_2_out, and_1_out);

  // Notes on the sheet:
  //   FULL ADDER
  //   CARRY
  //   SUM
endmodule
